// Logisim project rlt16hw4.circ as structural Verilog: 17 circuits, main circuit main
module main (
);

  wire alu_1_isneg, alu_1_iszero, ALUinB, and_1_out, and_2_out, blt, bne, Bsel, clk, controlled_buffer_1_out,
       controlled_buffer_2_out, DMwe, in, jal, JP, JR, keyboard_1_avail, multiplexer_12_out, not_1_out, out,
       Rdst, reset, Rwd, Rwe;
  wire [2:0] ALUop, multiplexer_3_out, multiplexer_4_out, multiplexer_5_out, multiplexer_6_out, Rd, Rs, Rt,
       shamt;
  wire [3:0] opcode;
  wire [5:0] immediate;
  wire [6:0] get_ascii_1_ascii, keyboard_1_data;
  wire [11:0] address;
  wire [15:0] alu_1_output, bit_extender_1_out, inRs, multiplexer_1_out, multiplexer_2_out,
       multiplexer_7_out, multiplexer_8_out, multiplexer_9_out, multiplexer_10_out, multiplexer_11_out,
       multiplexer_13_out, n16_bit_adder_1_out, n16_bit_adder_2_out, pc_1_output, pc_change_1_new_pc,
       ram_1_data, register_file_1_rs1val, register_file_1_rs2val, rom_1_data;

  // Probe on multiplexer_13_out
  // Probe on opcode
  opcode opcode_1 (
    .Opcode(opcode), .bne(bne), .RWe(Rwe), .JP(JP), .DMwe(DMwe), .Rwd(Rwd), .Rdst(Rdst), .ALUinB(ALUinB),
    .BSel(Bsel), .JR(JR), .jal(jal), .out(out), .ALUop_2(ALUop), .blt(blt), .in(in));  // open: ALUop
  PC pc_1 (.Reset(reset), .WE(1'b1), .\output (pc_1_output), .Input(multiplexer_13_out));
  // Probe on pc_1_output
  ROM #(.addrWidth(16), .dataWidth(16)) rom_1 (.addr(pc_1_output), .data(rom_1_data));  // open: sel
  // Probe on rom_1_data
  // Probe on ALUop
  Instruction_Decode instruction_decode_1 (
    .Input(rom_1_data), .Shamt(shamt), .Rd(Rd), .Rt(Rt), .Rs(Rs), .Opcode(opcode), .Immediate(immediate),
    .Address(address));
  _16_bit_adder u_16_bit_adder_1 (.a(16'h1), .b(pc_1_output), .out(n16_bit_adder_1_out), .Cin(1'b0));  // open: Cout
  // Probe on n16_bit_adder_1_out
  // Probe on shamt
  // Probe on Rd
  // Probe on Rt
  // Probe on Rs
  // Probe on opcode
  // Probe on immediate
  // Probe on address
  Clock clock_1 (.out(clk));
  Multiplexer #(.width(16), .enable("false")) multiplexer_1 (
    .in0(multiplexer_11_out), .in1(inRs), .out(multiplexer_1_out), .sel(in));
  Register_File register_file_1 (
    .in_2(reset), .in_3(Rwe), .RD(multiplexer_3_out), .RDval(multiplexer_2_out),
    .RS1val(register_file_1_rs1val), .RS1(Rs), .RS2val(register_file_1_rs2val), .RS2(multiplexer_6_out));
  Multiplexer #(.width(16), .enable("false")) multiplexer_2 (
    .in0(multiplexer_1_out), .in1(n16_bit_adder_1_out), .out(multiplexer_2_out), .sel(jal));
  // Probe on Rwe
  Multiplexer #(.width(3), .enable("false")) multiplexer_3 (
    .in0(multiplexer_5_out), .in1(3'b111), .out(multiplexer_3_out), .sel(jal));
  Multiplexer #(.width(3), .enable("false")) multiplexer_4 (.in0(Rd), .in1(Rs), .out(multiplexer_4_out), .sel(in));
  Keyboard keyboard_1 (
    .clk(controlled_buffer_1_out), .re(in), .clr(reset), .avail(keyboard_1_avail), .data(keyboard_1_data));
  assign controlled_buffer_1_out = keyboard_1_avail ? clk : 1'bz;  // Controlled_Buffer controlled_buffer_1
  Button u_reset (.out(reset));
  // Probe on multiplexer_3_out
  // Probe on Rs
  Multiplexer #(.width(3), .enable("false")) multiplexer_5 (
    .in0(multiplexer_4_out), .in1(Rt), .out(multiplexer_5_out), .sel(ALUinB));
  PC_change pc_change_1 (.PCval(pc_1_output), .address(address), .New_PC(pc_change_1_new_pc));
  // Probe on register_file_1_rs1val
  // Probe on register_file_1_rs2val
  // Probe on multiplexer_6_out
  Multiplexer #(.width(3), .enable("false")) multiplexer_6 (.in0(Rs), .in1(Rt), .out(multiplexer_6_out), .sel(Rdst));
  // Probe on Rt
  ascii_to_Rs ascii_to_rs_1 (.ascii(keyboard_1_data), .valid(keyboard_1_avail), .Rs(inRs));
  assign bit_extender_1_out = {{10{1'b0}}, immediate};  // Bit_Extender bit_extender_1
  // Probe on bit_extender_1_out
  Multiplexer #(.width(16), .enable("false")) multiplexer_7 (
    .in0(register_file_1_rs2val), .in1(bit_extender_1_out), .out(multiplexer_7_out), .sel(ALUinB));
  // Probe on bit_extender_1_out
  ALU alu_1 (
    .input1(register_file_1_rs1val), .input2(multiplexer_7_out), .Cin(1'b0), .shamt(shamt), .ALUop(ALUop),
    .Output(alu_1_output), .isZero(alu_1_iszero), .isNeg(alu_1_isneg));  // open: Overflow
  get_ascii get_ascii_1 (.Rs(register_file_1_rs1val), .Ascii(get_ascii_1_ascii));
  assign controlled_buffer_2_out = out ? clk : 1'bz;  // Controlled_Buffer controlled_buffer_2
  TTY tty_1 (.data(get_ascii_1_ascii), .clk(controlled_buffer_2_out), .we(out), .clr(reset));
  Multiplexer #(.width(16), .enable("false")) multiplexer_8 (
    .in0(n16_bit_adder_1_out), .in1(n16_bit_adder_2_out), .out(multiplexer_8_out), .sel(multiplexer_12_out));
  _16_bit_adder u_16_bit_adder_2 (
    .a(n16_bit_adder_1_out), .b(bit_extender_1_out), .out(n16_bit_adder_2_out), .Cin(1'b0));  // open: Cout
  // Probe on multiplexer_12_out
  // Probe on ALUop
  Multiplexer #(.width(16), .enable("false")) multiplexer_9 (
    .in0(multiplexer_8_out), .in1(pc_change_1_new_pc), .out(multiplexer_9_out), .sel(JP));
  // Probe on multiplexer_11_out
  // Probe on alu_1_output
  Multiplexer #(.width(16), .enable("false")) multiplexer_10 (
    .in0(multiplexer_9_out), .in1(register_file_1_rs1val), .out(multiplexer_10_out), .sel(JR));
  and and_1 (and_1_out, bne, bne, not_1_out);
  not not_1 (not_1_out, alu_1_iszero);
  Multiplexer #(.width(16), .enable("false")) multiplexer_11 (
    .in0(alu_1_output), .in1(ram_1_data), .out(multiplexer_11_out), .sel(Rwd));
  Multiplexer #(.enable("false")) multiplexer_12 (
    .in0(and_1_out), .in1(and_2_out), .out(multiplexer_12_out), .sel(Bsel));
  and and_2 (and_2_out, blt, alu_1_isneg);
  Multiplexer #(.width(16), .enable("false")) multiplexer_13 (
    .in0(multiplexer_10_out), .in1(register_file_1_rs1val), .out(multiplexer_13_out), .sel(jal));
  RAM #(.addrWidth(16), .dataWidth(16), .bus("separate")) ram_1 (
    .addr(alu_1_output), .din(register_file_1_rs2val), .data(ram_1_data), .str(DMwe), .clk(clk), .ld(Rwd),
    .clr(reset));  // open: sel

  // Notes on the sheet:
  //   Instruction Memory (ROM)
  //   contents of rom_1 (hex, n*v repeats v):
  //   245 482 1298 2698 3620 46a8 5a32 6a34 e200 f201 7040 80c4
  //   keyboard input
  //   bne (subtract)
  //   Data Memory (RAM)
  //   blt (subtract)
endmodule

// register
module Register (
  input  Reset,
  input  WE,
  input  [15:0] Input,
  output [15:0] \output 
);

  wire clk, clock_1_out;

  Clock clock_1 (.out(clock_1_out));
  buf buffer_1 (clk, clock_1_out);
  D_Flip_Flop d_ff_1 (.clk(clk), .D(Input[0]), .Q(\output [0]), .en(WE), .reset(Reset));  // open: Qn, preset
  D_Flip_Flop d_ff_2 (.clk(clk), .D(Input[1]), .Q(\output [1]), .en(WE), .reset(Reset));  // open: Qn, preset
  D_Flip_Flop d_ff_3 (.clk(clk), .D(Input[2]), .Q(\output [2]), .en(WE), .reset(Reset));  // open: Qn, preset
  D_Flip_Flop d_ff_4 (.clk(clk), .D(Input[3]), .Q(\output [3]), .en(WE), .reset(Reset));  // open: Qn, preset
  D_Flip_Flop d_ff_5 (.clk(clk), .D(Input[4]), .Q(\output [4]), .en(WE), .reset(Reset));  // open: Qn, preset
  D_Flip_Flop d_ff_6 (.clk(clk), .D(Input[5]), .Q(\output [5]), .en(WE), .reset(Reset));  // open: Qn, preset
  D_Flip_Flop d_ff_7 (.clk(clk), .D(Input[6]), .Q(\output [6]), .en(WE), .reset(Reset));  // open: Qn, preset
  D_Flip_Flop d_ff_8 (.clk(clk), .D(Input[7]), .Q(\output [7]), .en(WE), .reset(Reset));  // open: Qn, preset
  D_Flip_Flop d_ff_9 (.clk(clk), .D(Input[8]), .Q(\output [8]), .en(WE), .reset(Reset));  // open: Qn, preset
  D_Flip_Flop d_ff_10 (.clk(clk), .D(Input[9]), .Q(\output [9]), .en(WE), .reset(Reset));  // open: Qn, preset
  D_Flip_Flop d_ff_11 (.clk(clk), .D(Input[10]), .Q(\output [10]), .en(WE), .reset(Reset));  // open: Qn, preset
  D_Flip_Flop d_ff_12 (.clk(clk), .D(Input[11]), .Q(\output [11]), .en(WE), .reset(Reset));  // open: Qn, preset
  D_Flip_Flop d_ff_13 (.clk(clk), .D(Input[12]), .Q(\output [12]), .en(WE), .reset(Reset));  // open: Qn, preset
  D_Flip_Flop d_ff_14 (.clk(clk), .D(Input[13]), .Q(\output [13]), .en(WE), .reset(Reset));  // open: Qn, preset
  D_Flip_Flop d_ff_15 (.clk(clk), .D(Input[14]), .Q(\output [14]), .en(WE), .reset(Reset));  // open: Qn, preset
  D_Flip_Flop d_ff_16 (.clk(clk), .D(Input[15]), .Q(\output [15]), .en(WE), .reset(Reset));  // open: Qn, preset
endmodule

// RegFile
module Register_File (
  input  [15:0] RDval,
  input  in_2,
  input  in_3,
  input  [2:0] RS1,
  input  [2:0] RS2,
  input  [2:0] RD,
  output [15:0] RS1val,
  output [15:0] RS2val
);

  wire and_2_out, and_3_out, and_4_out, and_5_out, and_6_out, and_7_out, and_8_out, decoder_1_out0,
       decoder_1_out1, decoder_1_out2, decoder_1_out3, decoder_1_out4, decoder_1_out5, decoder_1_out6,
       decoder_1_out7;
  wire [15:0] register_1_output, register_2_output, register_3_output, register_4_output, register_5_output,
       register_6_output, register_7_output, register_8_output;

  Clock clock_1 ();  // open: out
  Decoder #(.select(3)) decoder_1 (
    .out0(decoder_1_out0), .out1(decoder_1_out1), .out2(decoder_1_out2), .out3(decoder_1_out3),
    .out4(decoder_1_out4), .out5(decoder_1_out5), .out6(decoder_1_out6), .out7(decoder_1_out7), .sel(RD),
    .en(in_3));
  // AND_Gate and_1 has open pins: in2=decoder_1_out0, in4=in_3, out=open
  and and_2 (and_2_out, decoder_1_out1, in_3);
  and and_3 (and_3_out, decoder_1_out2, decoder_1_out2, in_3);
  and and_4 (and_4_out, decoder_1_out3, in_3);
  and and_5 (and_5_out, decoder_1_out4, in_3);
  and and_6 (and_6_out, decoder_1_out5, in_3);
  and and_7 (and_7_out, decoder_1_out6, in_3);
  and and_8 (and_8_out, decoder_1_out7, in_3);
  Register register_1 (.Reset(in_2), .WE(1'b0), .\output (register_1_output), .Input(RDval));
  Register register_2 (.Reset(in_2), .WE(and_3_out), .\output (register_2_output), .Input(RDval));
  Register register_3 (.Reset(in_2), .WE(and_4_out), .\output (register_3_output), .Input(RDval));
  Register register_4 (.Reset(in_2), .WE(and_5_out), .\output (register_4_output), .Input(RDval));
  Register register_5 (.Reset(in_2), .WE(and_6_out), .\output (register_5_output), .Input(RDval));
  Register register_6 (.Reset(in_2), .WE(and_7_out), .\output (register_6_output), .Input(RDval));
  Register register_7 (.Reset(in_2), .WE(and_8_out), .\output (register_7_output), .Input(RDval));
  Register register_8 (.Reset(in_2), .WE(and_2_out), .\output (register_8_output), .Input(RDval));
  Multiplexer #(.select(3), .width(16), .enable("false")) multiplexer_1 (
    .in0(register_1_output), .in1(register_8_output), .in2(register_2_output), .in3(register_3_output),
    .in4(register_4_output), .in5(register_5_output), .in6(register_6_output), .in7(register_7_output),
    .out(RS1val), .sel(RS1));
  Multiplexer #(.select(3), .width(16), .enable("false")) multiplexer_2 (
    .in0(register_1_output), .in1(register_8_output), .in2(register_2_output), .in3(register_3_output),
    .in4(register_4_output), .in5(register_5_output), .in6(register_6_output), .in7(register_7_output),
    .out(RS2val), .sel(RS2));

  // Other names for the same wires on the sheet: Reset = in_2; WE = in_3
endmodule

module ALU (
  input  [2:0] shamt,
  input  [15:0] input1,
  input  [15:0] input2,
  input  Cin,
  input  [2:0] ALUop,
  output Overflow,
  output [15:0] Output,
  output isZero,
  output isNeg
);

  wire n16_bit_adder_1_cout, n16_bit_adder_2_cout;
  wire [14:0] multiplexer_1_out;
  wire [15:0] bit_extender_1_out, n16_bit_adder_1_out, n16_bit_adder_2_out, not_1_out, not_2_out,
       rotate_right_1_rotated, rotateleft_1_rotated, xor_1_out;

  assign not_1_out = ~input2;  // NOT_Gate not_1, 16 bits wide
  assign not_2_out = ~input1;  // NOT_Gate not_2, 16 bits wide
  Rotate_Right rotate_right_1 (.shamt(shamt), .original(input1), .rotated(rotate_right_1_rotated));
  RotateLeft rotateleft_1 (.shamt(shamt), .original(input1), .rotated(rotateleft_1_rotated));
  _16_bit_adder u_16_bit_adder_1 (
    .a(input1), .b(input2), .out(n16_bit_adder_1_out), .Cin(Cin), .Cout(n16_bit_adder_1_cout));
  _16_bit_adder u_16_bit_adder_2 (
    .a(input1), .b(not_1_out), .out(n16_bit_adder_2_out), .Cin(Cin), .Cout(n16_bit_adder_2_cout));
  assign xor_1_out = input1 ^ input2;  // XOR_Gate xor_1, 16 bits wide
  Multiplexer #(.select(3), .width(16), .enable("false")) multiplexer_1 (
    .in0(rotate_right_1_rotated), .in1(rotateleft_1_rotated), .in2(n16_bit_adder_1_out),
    .in3(n16_bit_adder_2_out), .in4(xor_1_out), .in5(not_2_out), .in6(input1),
    .out({isNeg, multiplexer_1_out}), .sel(ALUop));  // open: in7
  Multiplexer #(.select(3), .enable("false")) multiplexer_2 (
    .in0(1'b0), .in1(1'b0), .in2(n16_bit_adder_1_cout), .in3(n16_bit_adder_2_cout), .in4(1'b0), .in5(1'b0),
    .out(Overflow), .sel(ALUop));  // open: in6, in7
  assign bit_extender_1_out = {{15{1'b0}}, Overflow};  // Bit_Extender bit_extender_1
  _16_bit_adder u_16_bit_adder_3 (
    .a(bit_extender_1_out), .b({isNeg, multiplexer_1_out}), .out(Output), .Cin(1'b0));  // open: Cout
  nor nor_1 (isZero, multiplexer_1_out[0], multiplexer_1_out[1], multiplexer_1_out[2], multiplexer_1_out[3], multiplexer_1_out[4], multiplexer_1_out[5], multiplexer_1_out[6], multiplexer_1_out[7], multiplexer_1_out[8], multiplexer_1_out[9], multiplexer_1_out[10], multiplexer_1_out[11], multiplexer_1_out[12], multiplexer_1_out[13], multiplexer_1_out[14], isNeg);
endmodule

module _1_bit_adder (
  input  Cin,
  input  a,
  input  b,
  output sum,
  output Cout
);

  wire and_1_out, and_2_out, xor_1_out;

  and and_1 (and_1_out, a, a, b);
  xor xor_1 (xor_1_out, a, b);
  and and_2 (and_2_out, xor_1_out, Cin);
  xor xor_2 (sum, Cin, xor_1_out);
  or or_1 (Cout, and_2_out, and_1_out);
endmodule

module Instruction_Decode (
  input  [15:0] Input,
  output [2:0] Shamt,
  output [2:0] Rd,
  output [2:0] Rt,
  output [2:0] Rs,
  output [3:0] Opcode,
  output [5:0] Immediate,
  output [11:0] Address
);


  assign Address = Input[11:0];
  assign Immediate = Input[5:0];
  assign Opcode = Input[15:12];
  assign Rd = Input[5:3];
  assign Rs = Input[11:9];
  assign Rt = Input[8:6];
  assign Shamt = Input[2:0];

  // Notes on the sheet:
  //   R Type
  //   I Type
  //   J Type
endmodule

module _1_bit_shifter (
  input  [15:0] Input,
  output [15:0] Output
);

  Multiplexer #(.enable("false")) multiplexer_1 (.in0(Input[15]), .in1(Input[14]), .out(Output[15]), .sel(1'b1));
  Multiplexer #(.enable("false")) multiplexer_2 (.in0(Input[14]), .in1(Input[13]), .out(Output[14]), .sel(1'b1));
  Multiplexer #(.enable("false")) multiplexer_3 (.in0(Input[13]), .in1(Input[12]), .out(Output[13]), .sel(1'b1));
  Multiplexer #(.enable("false")) multiplexer_4 (.in0(Input[12]), .in1(Input[11]), .out(Output[12]), .sel(1'b1));
  Multiplexer #(.enable("false")) multiplexer_5 (.in0(Input[11]), .in1(Input[10]), .out(Output[11]), .sel(1'b1));
  Multiplexer #(.enable("false")) multiplexer_6 (.in0(Input[10]), .in1(Input[9]), .out(Output[10]), .sel(1'b1));
  Multiplexer #(.enable("false")) multiplexer_7 (.in0(Input[9]), .in1(Input[8]), .out(Output[9]), .sel(1'b1));
  Multiplexer #(.enable("false")) multiplexer_8 (.in0(Input[8]), .in1(Input[7]), .out(Output[8]), .sel(1'b1));
  Multiplexer #(.enable("false")) multiplexer_9 (.in0(Input[7]), .in1(Input[6]), .out(Output[7]), .sel(1'b1));
  Multiplexer #(.enable("false")) multiplexer_10 (.in0(Input[6]), .in1(Input[5]), .out(Output[6]), .sel(1'b1));
  Multiplexer #(.enable("false")) multiplexer_11 (.in0(Input[5]), .in1(Input[4]), .out(Output[5]), .sel(1'b1));
  Multiplexer #(.enable("false")) multiplexer_12 (.in0(Input[4]), .in1(Input[3]), .out(Output[4]), .sel(1'b1));
  Multiplexer #(.enable("false")) multiplexer_13 (.in0(Input[3]), .in1(Input[2]), .out(Output[3]), .sel(1'b1));
  Multiplexer #(.enable("false")) multiplexer_14 (.in0(Input[2]), .in1(Input[1]), .out(Output[2]), .sel(1'b1));
  Multiplexer #(.enable("false")) multiplexer_15 (.in0(Input[1]), .in1(Input[0]), .out(Output[1]), .sel(1'b1));
  Multiplexer #(.enable("false")) multiplexer_16 (.in0(Input[0]), .in1(1'b0), .out(Output[0]), .sel(1'b1));
endmodule

module ROL (
  input  [15:0] Input,
  input  enable,
  output [15:0] Output
);

  Multiplexer #(.enable("false")) multiplexer_1 (.in0(Input[15]), .in1(Input[14]), .out(Output[15]), .sel(enable));
  Multiplexer #(.enable("false")) multiplexer_2 (.in0(Input[14]), .in1(Input[13]), .out(Output[14]), .sel(enable));
  Multiplexer #(.enable("false")) multiplexer_3 (.in0(Input[13]), .in1(Input[12]), .out(Output[13]), .sel(enable));
  Multiplexer #(.enable("false")) multiplexer_4 (.in0(Input[12]), .in1(Input[11]), .out(Output[12]), .sel(enable));
  Multiplexer #(.enable("false")) multiplexer_5 (.in0(Input[11]), .in1(Input[10]), .out(Output[11]), .sel(enable));
  Multiplexer #(.enable("false")) multiplexer_6 (.in0(Input[10]), .in1(Input[9]), .out(Output[10]), .sel(enable));
  Multiplexer #(.enable("false")) multiplexer_7 (.in0(Input[9]), .in1(Input[8]), .out(Output[9]), .sel(enable));
  Multiplexer #(.enable("false")) multiplexer_8 (.in0(Input[8]), .in1(Input[7]), .out(Output[8]), .sel(enable));
  Multiplexer #(.enable("false")) multiplexer_9 (.in0(Input[7]), .in1(Input[6]), .out(Output[7]), .sel(enable));
  Multiplexer #(.enable("false")) multiplexer_10 (.in0(Input[6]), .in1(Input[5]), .out(Output[6]), .sel(enable));
  Multiplexer #(.enable("false")) multiplexer_11 (.in0(Input[5]), .in1(Input[4]), .out(Output[5]), .sel(enable));
  Multiplexer #(.enable("false")) multiplexer_12 (.in0(Input[4]), .in1(Input[3]), .out(Output[4]), .sel(enable));
  Multiplexer #(.enable("false")) multiplexer_13 (.in0(Input[3]), .in1(Input[2]), .out(Output[3]), .sel(enable));
  Multiplexer #(.enable("false")) multiplexer_14 (.in0(Input[2]), .in1(Input[1]), .out(Output[2]), .sel(enable));
  Multiplexer #(.enable("false")) multiplexer_15 (.in0(Input[1]), .in1(Input[0]), .out(Output[1]), .sel(enable));
  Multiplexer #(.enable("false")) multiplexer_16 (.in0(Input[0]), .in1(Input[15]), .out(Output[0]), .sel(enable));
endmodule

module RotateLeft (
  input  [2:0] shamt,
  input  [15:0] original,
  output [15:0] rotated
);

  wire [15:0] rol_1_output, rol_2_output, rol_3_output, rol_4_output, rol_5_output, rol_6_output;

  ROL rol_1 (.Output(rol_1_output), .Input(original), .enable(shamt[0]));
  ROL rol_2 (.Output(rol_2_output), .Input(rol_1_output), .enable(shamt[1]));
  ROL rol_3 (.Output(rol_3_output), .Input(rol_2_output), .enable(shamt[1]));
  ROL rol_4 (.Output(rol_4_output), .Input(rol_3_output), .enable(shamt[2]));
  ROL rol_5 (.Output(rol_5_output), .Input(rol_4_output), .enable(shamt[2]));
  ROL rol_6 (.Output(rol_6_output), .Input(rol_5_output), .enable(shamt[2]));
  ROL rol_7 (.Output(rotated), .Input(rol_6_output), .enable(shamt[2]));

  // Other names for the same wires on the sheet: bit1 = shamt[0]; bit2 = shamt[1]; bit3 = shamt[2]
endmodule

module _16_bit_adder (
  input  [15:0] a,
  input  [15:0] b,
  input  Cin,
  output [15:0] out,
  output Cout
);

  wire n1_bit_adder_1_cout, n1_bit_adder_2_cout, n1_bit_adder_3_cout, n1_bit_adder_4_cout,
       n1_bit_adder_5_cout, n1_bit_adder_6_cout, n1_bit_adder_7_cout, n1_bit_adder_8_cout,
       n1_bit_adder_9_cout, n1_bit_adder_10_cout, n1_bit_adder_11_cout, n1_bit_adder_12_cout,
       n1_bit_adder_13_cout, n1_bit_adder_14_cout, n1_bit_adder_15_cout;

  _1_bit_adder u_1_bit_adder_1 (.Cin(Cin), .a(a[0]), .b(b[0]), .sum(out[0]), .Cout(n1_bit_adder_1_cout));
  _1_bit_adder u_1_bit_adder_2 (
    .Cin(n1_bit_adder_7_cout), .a(a[4]), .b(b[4]), .sum(out[4]), .Cout(n1_bit_adder_2_cout));
  _1_bit_adder u_1_bit_adder_3 (
    .Cin(n1_bit_adder_1_cout), .a(a[1]), .b(b[1]), .sum(out[1]), .Cout(n1_bit_adder_3_cout));
  _1_bit_adder u_1_bit_adder_4 (
    .Cin(n1_bit_adder_2_cout), .a(a[5]), .b(b[5]), .sum(out[5]), .Cout(n1_bit_adder_4_cout));
  _1_bit_adder u_1_bit_adder_5 (
    .Cin(n1_bit_adder_3_cout), .a(a[2]), .b(b[2]), .sum(out[2]), .Cout(n1_bit_adder_5_cout));
  _1_bit_adder u_1_bit_adder_6 (
    .Cin(n1_bit_adder_4_cout), .a(a[6]), .b(b[6]), .sum(out[6]), .Cout(n1_bit_adder_6_cout));
  _1_bit_adder u_1_bit_adder_7 (
    .Cin(n1_bit_adder_5_cout), .a(a[3]), .b(b[3]), .sum(out[3]), .Cout(n1_bit_adder_7_cout));
  _1_bit_adder u_1_bit_adder_8 (
    .Cin(n1_bit_adder_6_cout), .a(a[7]), .b(b[7]), .sum(out[7]), .Cout(n1_bit_adder_8_cout));
  _1_bit_adder u_1_bit_adder_9 (
    .Cin(n1_bit_adder_8_cout), .a(a[8]), .b(b[8]), .sum(out[8]), .Cout(n1_bit_adder_9_cout));
  _1_bit_adder u_1_bit_adder_10 (
    .Cin(n1_bit_adder_15_cout), .a(a[12]), .b(b[12]), .sum(out[12]), .Cout(n1_bit_adder_10_cout));
  _1_bit_adder u_1_bit_adder_11 (
    .Cin(n1_bit_adder_9_cout), .a(a[9]), .b(b[9]), .sum(out[9]), .Cout(n1_bit_adder_11_cout));
  _1_bit_adder u_1_bit_adder_12 (
    .Cin(n1_bit_adder_10_cout), .a(a[13]), .b(b[13]), .sum(out[13]), .Cout(n1_bit_adder_12_cout));
  _1_bit_adder u_1_bit_adder_13 (
    .Cin(n1_bit_adder_11_cout), .a(a[10]), .b(b[10]), .sum(out[10]), .Cout(n1_bit_adder_13_cout));
  _1_bit_adder u_1_bit_adder_14 (
    .Cin(n1_bit_adder_12_cout), .a(a[14]), .b(b[14]), .sum(out[14]), .Cout(n1_bit_adder_14_cout));
  _1_bit_adder u_1_bit_adder_15 (
    .Cin(n1_bit_adder_13_cout), .a(a[11]), .b(b[11]), .sum(out[11]), .Cout(n1_bit_adder_15_cout));
  _1_bit_adder u_1_bit_adder_16 (.Cin(n1_bit_adder_14_cout), .a(a[15]), .b(b[15]), .sum(out[15]), .Cout(Cout));

  // Other names for the same wires on the sheet: sum0 = out[0]; sum1 = out[1]; sum2 = out[2]; sum3 = out[3];
  //   sum4 = out[4]; sum5 = out[5]; sum6 = out[6]; sum7 = out[7]; sum8 = out[8]; sum9 = out[9]; sum10 = out[10];
  //   sum11 = out[11]; sum12 = out[12]; sum13 = out[13]; sum14 = out[14]; sum15 = out[15]
endmodule

module ror1 (
  input  [15:0] Input,
  input  enable,
  output [15:0] Output
);

  Multiplexer #(.enable("false")) multiplexer_1 (.in0(Input[0]), .in1(Input[1]), .out(Output[0]), .sel(enable));
  Multiplexer #(.enable("false")) multiplexer_2 (.in0(Input[1]), .in1(Input[2]), .out(Output[1]), .sel(enable));
  Multiplexer #(.enable("false")) multiplexer_3 (.in0(Input[2]), .in1(Input[3]), .out(Output[2]), .sel(enable));
  Multiplexer #(.enable("false")) multiplexer_4 (.in0(Input[3]), .in1(Input[4]), .out(Output[3]), .sel(enable));
  Multiplexer #(.enable("false")) multiplexer_5 (.in0(Input[4]), .in1(Input[5]), .out(Output[4]), .sel(enable));
  Multiplexer #(.enable("false")) multiplexer_6 (.in0(Input[5]), .in1(Input[6]), .out(Output[5]), .sel(enable));
  Multiplexer #(.enable("false")) multiplexer_7 (.in0(Input[6]), .in1(Input[7]), .out(Output[6]), .sel(enable));
  Multiplexer #(.enable("false")) multiplexer_8 (.in0(Input[7]), .in1(Input[8]), .out(Output[7]), .sel(enable));
  Multiplexer #(.enable("false")) multiplexer_9 (.in0(Input[8]), .in1(Input[9]), .out(Output[8]), .sel(enable));
  Multiplexer #(.enable("false")) multiplexer_10 (.in0(Input[9]), .in1(Input[10]), .out(Output[9]), .sel(enable));
  Multiplexer #(.enable("false")) multiplexer_11 (.in0(Input[10]), .in1(Input[11]), .out(Output[10]), .sel(enable));
  Multiplexer #(.enable("false")) multiplexer_12 (.in0(Input[11]), .in1(Input[12]), .out(Output[11]), .sel(enable));
  Multiplexer #(.enable("false")) multiplexer_13 (.in0(Input[12]), .in1(Input[13]), .out(Output[12]), .sel(enable));
  Multiplexer #(.enable("false")) multiplexer_14 (.in0(Input[13]), .in1(Input[14]), .out(Output[13]), .sel(enable));
  Multiplexer #(.enable("false")) multiplexer_15 (.in0(Input[14]), .in1(Input[15]), .out(Output[14]), .sel(enable));
  Multiplexer #(.enable("false")) multiplexer_16 (.in0(Input[15]), .in1(Input[0]), .out(Output[15]), .sel(enable));
endmodule

module Rotate_Right (
  input  [2:0] shamt,
  input  [15:0] original,
  output [15:0] rotated
);

  wire [15:0] ror1_1_output, ror1_2_output, ror1_3_output, ror1_4_output, ror1_5_output, ror1_6_output;

  ror1 ror1_1 (.Output(ror1_1_output), .Input(original), .enable(shamt[0]));
  ror1 ror1_2 (.Output(ror1_2_output), .Input(ror1_1_output), .enable(shamt[1]));
  ror1 ror1_3 (.Output(ror1_3_output), .Input(ror1_2_output), .enable(shamt[1]));
  ror1 ror1_4 (.Output(ror1_4_output), .Input(ror1_3_output), .enable(shamt[2]));
  ror1 ror1_5 (.Output(ror1_5_output), .Input(ror1_4_output), .enable(shamt[2]));
  ror1 ror1_6 (.Output(ror1_6_output), .Input(ror1_5_output), .enable(shamt[2]));
  ror1 ror1_7 (.Output(rotated), .Input(ror1_6_output), .enable(shamt[2]));

  // Other names for the same wires on the sheet: bit1 = shamt[0]; bit2 = shamt[1]; bit3 = shamt[2]
endmodule

module opcode (
  input  [3:0] Opcode,
  input  [2:0] ALUop,
  output Rdst,
  output blt,
  output JR,
  output bne,
  output Rwd,
  output jal,
  output out,
  output RWe,
  output JP,
  output DMwe,
  output ALUinB,
  output in,
  output BSel,
  output [2:0] ALUop_2
);

  wire add_out, decoder_1_out0, decoder_1_out1, decoder_1_out2, decoder_1_out3, decoder_1_out4,
       decoder_1_out5, decoder_1_out6, decoder_1_out11, subtract_out;

  Decoder #(.select(4), .enable("false")) decoder_1 (
    .out0(decoder_1_out0), .out1(decoder_1_out1), .out2(decoder_1_out2), .out3(decoder_1_out3),
    .out4(decoder_1_out4), .out5(decoder_1_out5), .out6(decoder_1_out6), .out7(Rwd), .out8(DMwe), .out9(bne),
    .out10(blt), .out11(decoder_1_out11), .out12(JR), .out13(jal), .out14(in), .out15(out), .sel(Opcode));
  or or_1 (RWe, decoder_1_out0, decoder_1_out1, decoder_1_out2, decoder_1_out3, decoder_1_out4, decoder_1_out5, decoder_1_out6, Rwd, jal, in);
  or or_2 (JP, jal, JR, decoder_1_out11);
  not not_1 (Rdst, Rwd);
  or or_3 (ALUinB, decoder_1_out0, Rwd, DMwe);
  or add (add_out, decoder_1_out0, DMwe, Rwd, decoder_1_out1, JR, decoder_1_out11);
  or or_4 (ALUop_2[1], add_out, subtract_out);
  or subtract (subtract_out, decoder_1_out2, bne, blt);
  or or_5 (ALUop_2[0], subtract_out, decoder_1_out5, decoder_1_out3);
  or or_6 (ALUop_2[2], decoder_1_out3, decoder_1_out4);

  assign BSel = blt;

  // Notes on the sheet:
  //   add
  //   sub
  //   not
  //   xor
  //   rol
  //   ror
  //   lw
  //   sw
  //   bne
  //   blt
  //   j
  //   jr
  //   jal
  //   input
  //   output
endmodule

module PC (
  input  Reset,
  input  WE,
  input  [15:0] Input,
  output [15:0] \output 
);

  wire clk;

  Clock clock_1 (.out(clk));
  D_Flip_Flop d_ff_1 (.clk(clk), .D(Input[0]), .Q(\output [0]), .en(WE), .reset(Reset));  // open: Qn, preset
  D_Flip_Flop d_ff_2 (.clk(clk), .D(Input[1]), .Q(\output [1]), .en(WE), .reset(Reset));  // open: Qn, preset
  D_Flip_Flop d_ff_3 (.clk(clk), .D(Input[2]), .Q(\output [2]), .en(WE), .reset(Reset));  // open: Qn, preset
  D_Flip_Flop d_ff_4 (.clk(clk), .D(Input[3]), .Q(\output [3]), .en(WE), .reset(Reset));  // open: Qn, preset
  D_Flip_Flop d_ff_5 (.clk(clk), .D(Input[4]), .Q(\output [4]), .en(WE), .reset(Reset));  // open: Qn, preset
  D_Flip_Flop d_ff_6 (.clk(clk), .D(Input[5]), .Q(\output [5]), .en(WE), .reset(Reset));  // open: Qn, preset
  D_Flip_Flop d_ff_7 (.clk(clk), .D(Input[6]), .Q(\output [6]), .en(WE), .reset(Reset));  // open: Qn, preset
  D_Flip_Flop d_ff_8 (.clk(clk), .D(Input[7]), .Q(\output [7]), .en(WE), .reset(Reset));  // open: Qn, preset
  D_Flip_Flop d_ff_9 (.clk(clk), .D(Input[8]), .Q(\output [8]), .en(WE), .reset(Reset));  // open: Qn, preset
  D_Flip_Flop d_ff_10 (.clk(clk), .D(Input[9]), .Q(\output [9]), .en(WE), .reset(Reset));  // open: Qn, preset
  D_Flip_Flop d_ff_11 (.clk(clk), .D(Input[10]), .Q(\output [10]), .en(WE), .reset(Reset));  // open: Qn, preset
  D_Flip_Flop d_ff_12 (.clk(clk), .D(Input[11]), .Q(\output [11]), .en(WE), .reset(Reset));  // open: Qn, preset
  D_Flip_Flop d_ff_13 (.clk(clk), .D(Input[12]), .Q(\output [12]), .en(WE), .reset(Reset));  // open: Qn, preset
  D_Flip_Flop d_ff_14 (.clk(clk), .D(Input[13]), .Q(\output [13]), .en(WE), .reset(Reset));  // open: Qn, preset
  D_Flip_Flop d_ff_15 (.clk(clk), .D(Input[14]), .Q(\output [14]), .en(WE), .reset(Reset));  // open: Qn, preset
  D_Flip_Flop d_ff_16 (.clk(clk), .D(Input[15]), .Q(\output [15]), .en(WE), .reset(Reset));  // open: Qn, preset
endmodule

module PC_change (
  input  [15:0] PCval,
  input  [11:0] address,
  output [15:0] New_PC
);


  assign New_PC = {PCval[15:12], address};
endmodule

module get_ascii (
  input  [15:0] Rs,
  output [6:0] Ascii
);


  assign Ascii = Rs[6:0];
endmodule

module ascii_to_Rs (
  input  [6:0] ascii,
  input  valid,
  output [15:0] Rs
);

  not not_1 (Rs[7], valid);

  assign {Rs[15:8], Rs[6:0]} = {{8{1'b0}}, ascii};
endmodule
